// Logisim project P1.circ as structural Verilog: 15 circuits, main circuit ALU32
module LeftShift32 (
  input  [31:0] B,
  input  [4:0] Sa,
  input  Cin,
  output [31:0] C
);

  wire [31:0] leftshift1_1_c, leftshift2_1_c, leftshift4_1_c, leftshift8_1_c, leftshift16_1_c,
       multiplexer_1_out, multiplexer_2_out, multiplexer_3_out, multiplexer_4_out;

  LeftShift1 leftshift1_1 (.B(B), .Cin(Cin), .C(leftshift1_1_c));
  Multiplexer #(.width(32), .enable("false")) multiplexer_1 (
    .in0(B), .in1(leftshift1_1_c), .out(multiplexer_1_out), .sel(Sa[0]));
  LeftShift2 leftshift2_1 (.B(multiplexer_1_out), .Cin(Cin), .C(leftshift2_1_c));
  Multiplexer #(.width(32), .enable("false")) multiplexer_2 (
    .in0(multiplexer_1_out), .in1(leftshift2_1_c), .out(multiplexer_2_out), .sel(Sa[1]));
  Multiplexer #(.width(32), .enable("false")) multiplexer_3 (
    .in0(multiplexer_2_out), .in1(leftshift4_1_c), .out(multiplexer_3_out), .sel(Sa[2]));
  LeftShift4 leftshift4_1 (.B(multiplexer_2_out), .Cin(Cin), .C(leftshift4_1_c));
  Multiplexer #(.width(32), .enable("false")) multiplexer_4 (
    .in0(multiplexer_3_out), .in1(leftshift8_1_c), .out(multiplexer_4_out), .sel(Sa[3]));
  LeftShift8 leftshift8_1 (.B(multiplexer_3_out), .Cin(Cin), .C(leftshift8_1_c));
  Multiplexer #(.width(32), .enable("false")) multiplexer_5 (
    .in0(multiplexer_4_out), .in1(leftshift16_1_c), .out(C), .sel(Sa[4]));
  LeftShift16 leftshift16_1 (.B(multiplexer_4_out), .Cin(Cin), .C(leftshift16_1_c));
endmodule

module Add32 (
  input  Cin,
  input  [31:0] A,
  input  [31:0] B,
  output [31:0] C,
  output V
);

  wire add16_1_v;

  Add16 add16_1 (.Cin(Cin), .A(A[15:0]), .B(B[15:0]), .C(C[15:0]), .V(add16_1_v));
  Add16 add16_2 (.Cin(add16_1_v), .A(A[31:16]), .B(B[31:16]), .C(C[31:16]), .V(V));
endmodule

module ALU32 (
  input  [31:0] A,
  input  [31:0] B,
  input  [3:0] Op,
  input  [4:0] Sa,
  output [31:0] C,
  output V
);

  Multiplexer #(.enable("false")) multiplexer_1 (.sel(Op[3]));  // open: in0, in1, out
endmodule

module Add1 (
  input  A,
  input  B,
  input  Cin,
  output C,
  output V
);

  wire and_1_out, and_2_out, xor_1_out;

  xor xor_1 (xor_1_out, A, B);
  xor xor_2 (C, xor_1_out, Cin);
  and and_1 (and_1_out, xor_1_out, Cin);
  and and_2 (and_2_out, A, B);
  or or_1 (V, and_1_out, and_2_out);
endmodule

module Add2 (
  input  Cin,
  input  [1:0] A,
  input  [1:0] B,
  output [1:0] C,
  output V
);

  wire add1_1_v;

  Add1 add1_1 (.A(A[0]), .B(B[0]), .Cin(Cin), .C(C[0]), .V(add1_1_v));
  Add1 add1_2 (.A(A[1]), .B(B[1]), .Cin(add1_1_v), .C(C[1]), .V(V));
endmodule

module Add4 (
  input  Cin,
  input  [3:0] A,
  input  [3:0] B,
  output [3:0] C,
  output V
);

  wire add2_1_v;

  Add2 add2_1 (.Cin(Cin), .A(A[1:0]), .B(B[1:0]), .C(C[1:0]), .V(add2_1_v));
  Add2 add2_2 (.Cin(add2_1_v), .A(A[3:2]), .B(B[3:2]), .C(C[3:2]), .V(V));
endmodule

module Add8 (
  input  Cin,
  input  [7:0] A,
  input  [7:0] B,
  output [7:0] C,
  output V
);

  wire add4_1_v;

  Add4 add4_1 (.Cin(Cin), .A(A[3:0]), .B(B[3:0]), .C(C[3:0]), .V(add4_1_v));
  Add4 add4_2 (.Cin(add4_1_v), .A(A[7:4]), .B(B[7:4]), .C(C[7:4]), .V(V));
endmodule

module Add16 (
  input  Cin,
  input  [15:0] A,
  input  [15:0] B,
  output [15:0] C,
  output V
);

  wire add8_1_v;

  Add8 add8_1 (.Cin(Cin), .A(A[7:0]), .B(B[7:0]), .C(C[7:0]), .V(add8_1_v));
  Add8 add8_2 (.Cin(add8_1_v), .A(A[15:8]), .B(B[15:8]), .C(C[15:8]), .V(V));
endmodule

module LeftShift1 (
  input  [31:0] B,
  input  Cin,
  output [31:0] C
);


  assign C = {B[30:0], Cin};
endmodule

module LeftShift2 (
  input  [31:0] B,
  input  Cin,
  output [31:0] C
);


  assign C = {B[29:0], {2{Cin}}};
endmodule

module LeftShift4 (
  input  [31:0] B,
  input  Cin,
  output [31:0] C
);


  assign C = {B[27:0], {4{Cin}}};
endmodule

module LeftShift8 (
  input  [31:0] B,
  input  Cin,
  output [31:0] C
);


  assign C = {B[23:0], {8{Cin}}};
endmodule

module LeftShift16 (
  input  [31:0] B,
  input  Cin,
  output [31:0] C
);


  assign C = {B[15:0], {16{Cin}}};
endmodule

module Logic (
  input  [31:0] A,
  input  [31:0] B,
  input  [1:0] Op,
  output [31:0] C
);

  wire [31:0] and_1_out, nor_1_out, or_1_out, xor_1_out;

  assign and_1_out = B & A;  // AND_Gate and_1, 32 bits wide
  assign or_1_out = B | A;  // OR_Gate or_1, 32 bits wide
  assign xor_1_out = B ^ A;  // XOR_Gate xor_1, 32 bits wide
  assign nor_1_out = ~(B | A);  // NOR_Gate nor_1, 32 bits wide
  Multiplexer #(.select(2), .width(32), .enable("false")) multiplexer_1 (
    .in0(and_1_out), .in1(or_1_out), .in2(xor_1_out), .in3(nor_1_out), .out(C), .sel(Op));
endmodule

module RightShift32 (
  input  [31:0] B,
  input  [4:0] Sa,
  input  Cin,
  output [31:0] C
);

  LeftShift32 leftshift32_1 (
    .B({B[0], B[1], B[2], B[3], B[4], B[5], B[6], B[7], B[8], B[9], B[10], B[11], B[12], B[13], B[14], B[15], B[16], B[17], B[18], B[19], B[20], B[21], B[22], B[23], B[24], B[25], B[26], B[27], B[28], B[29], B[30], B[31]}),
    .Sa(Sa), .Cin(Cin),
    .C({C[0], C[1], C[2], C[3], C[4], C[5], C[6], C[7], C[8], C[9], C[10], C[11], C[12], C[13], C[14], C[15], C[16], C[17], C[18], C[19], C[20], C[21], C[22], C[23], C[24], C[25], C[26], C[27], C[28], C[29], C[30], C[31]}));
endmodule
